// Logisim project processador_viw.circ as structural Verilog
module ula (
  input  [7:0] entradaA,
  input  [7:0] entradaB,
  input  [2:0] OpULA,
  output [7:0] saidaULA
);

  wire nor_1_out, or_2_out;
  wire [7:0] adder_1_out, adder_2_out, bit_extender_1_out, multiplexer_1_out, multiplexer_2_out, or_1_out,
       shifter_1_out, shifter_2_out, subtractor_1_out;

  Adder adder_1 (.a(entradaA), .b(entradaB), .out(adder_1_out));  // open: cin, cout
  Subtractor subtractor_1 (.a(entradaA), .b(entradaB), .out(subtractor_1_out));  // open: bin, bout
  assign or_1_out = entradaA | entradaB;  // OR_Gate or_1, 8 bits wide
  Shifter shifter_1 (.in(entradaA), .\dist (entradaB[2:0]), .out(shifter_1_out));
  or or_2 (or_2_out, entradaB[3], entradaB[4], entradaB[5], entradaB[6], entradaB[7]);
  Shifter #(.shift("lr")) shifter_2 (.in(entradaA), .\dist (entradaB[2:0]), .out(shifter_2_out));
  Adder adder_2 (.a(entradaA), .b(8'h1), .out(adder_2_out));  // open: cin, cout
  nor nor_1 (nor_1_out, entradaB[0], entradaB[1], entradaB[2], entradaB[3], entradaB[4], entradaB[5], entradaB[6], entradaB[7]);
  Multiplexer #(.width(8)) multiplexer_1 (
    .in0(shifter_1_out), .in1({8{1'b0}}), .out(multiplexer_1_out), .sel(or_2_out));
  Multiplexer #(.width(8)) multiplexer_2 (
    .in0({8{1'b0}}), .in1(shifter_2_out), .out(multiplexer_2_out), .sel(or_2_out));
  assign bit_extender_1_out = {{7{nor_1_out}}, nor_1_out};  // Bit_Extender bit_extender_1
  Multiplexer #(.select(3), .width(8)) multiplexer_3 (
    .in0(adder_1_out), .in1(subtractor_1_out), .in2(adder_2_out), .in3(or_1_out), .in4(bit_extender_1_out),
    .in5(multiplexer_1_out), .in6(multiplexer_2_out), .out(saidaULA), .sel(OpULA));  // open: in7
endmodule

module control (
  input  [3:0] InstrL1,
  input  [3:0] InstrL2,
  input  [3:0] InstrL3,
  input  [3:0] InstrL4,
  output MemWriteL1,
  output MemrRead,
  output MuxL1Src,
  output RegWriteL1,
  output Sig_BRZR,
  output Sig_BRZI,
  output Sig_JR,
  output Sig_BNZR,
  output RegWriteULA1,
  output [2:0] OpULA1,
  output RegWriteULA2,
  output [2:0] OpULA2
);

  controlL1 controll1_1 (
    .Op3(InstrL1[3]), .Op2(InstrL1[2]), .Op1(InstrL1[1]), .Op0(InstrL1[0]), .MemWriteL1(MemWriteL1),
    .MemRead(MemrRead), .MuxL1Src(MuxL1Src), .RegWriteL1(RegWriteL1));
  controlL2 controll2_1 (
    .Op3(InstrL2[0]), .Op2(InstrL2[1]), .Op1(InstrL2[2]), .Op0(InstrL2[3]), .Sig_BRZR(Sig_BRZR),
    .Sig_BRZI(Sig_BRZI), .Sig_JR(Sig_JR), .Sig_BNZR(Sig_BNZR));
  controlL3L4 controll3l4_1 (
    .ULA1(InstrL3), .ULA2(InstrL4), .RegWriteULA1(RegWriteULA1), .OpULA1(OpULA1),
    .RegWriteULA2(RegWriteULA2), .OpULA2(OpULA2));
endmodule

module move (
  input  [7:0] r0,
  input  [3:0] imm,
  output [7:0] movH,
  output [7:0] movL
);


  assign movH = r0;
  assign movL = {r0[7:4], imm};
endmodule

module mem (
);

  // DualRAM dualram_1: pin names not known
endmodule

module controlL1 (
  input  Op3,
  input  Op2,
  input  Op1,
  input  Op0,
  output MemWriteL1,
  output MemRead,
  output MuxL1Src,
  output RegWriteL1
);

  wire and_4_out, and_5_out, not_1_out, not_2_out, not_3_out;

  not not_1 (not_1_out, Op3);
  not not_2 (not_2_out, Op1);
  not not_3 (not_3_out, Op0);
  and and_1 (MemWriteL1, not_1_out, Op2, not_2_out, Op0);
  and and_2 (MemRead, not_1_out, Op2, not_2_out, not_3_out);
  and and_3 (MuxL1Src, not_1_out, Op2, Op1);
  and and_4 (and_4_out, not_1_out, Op2, not_3_out);
  and and_5 (and_5_out, not_1_out, Op2, Op1);
  or or_1 (RegWriteL1, and_4_out, and_5_out);
endmodule

module controlL2 (
  input  Op3,
  input  Op2,
  input  Op1,
  input  Op0,
  output Sig_BRZR,
  output Sig_BRZI,
  output Sig_JR,
  output Sig_BNZR
);

  wire not_1_out, not_2_out, not_3_out, not_4_out;

  not not_1 (not_1_out, Op3);
  not not_2 (not_2_out, Op2);
  not not_3 (not_3_out, Op1);
  not not_4 (not_4_out, Op0);
  and and_1 (Sig_BRZR, not_1_out, not_2_out, not_3_out, not_4_out);
  and and_2 (Sig_BRZI, not_1_out, not_2_out, not_3_out, Op0);
  and and_3 (Sig_JR, not_1_out, not_2_out, Op1, not_4_out);
  and and_4 (Sig_BNZR, not_1_out, not_2_out, Op1, Op0);
endmodule

module controlL3L4 (
  input  [3:0] ULA1,
  input  [3:0] ULA2,
  output RegWriteULA1,
  output [2:0] OpULA1,
  output RegWriteULA2,
  output [2:0] OpULA2
);

  wire nand_1_out, nand_2_out;

  nand nand_1 (nand_1_out, ULA1[0], ULA1[1], ULA1[2]);
  nand nand_2 (nand_2_out, ULA2[0], ULA2[1], ULA2[2]);
  and and_1 (RegWriteULA1, nand_1_out, ULA1[3]);
  and and_2 (RegWriteULA2, nand_2_out, ULA2[3]);
  Multiplexer #(.width(3)) multiplexer_1 (.in0(3'b000), .in1(ULA2[2:0]), .out(OpULA2), .sel(RegWriteULA2));
  Multiplexer #(.width(3)) multiplexer_2 (.in0(3'b000), .in1(ULA1[2:0]), .out(OpULA1), .sel(RegWriteULA1));
endmodule
